# Fritzing sketch Botsitos BT (saved by Fritzing 0.9.3b)

parts:
  Componente1 = Arduino Nano (Rev3.0)
  L298N1 = L298N DC motor driver
  BAT1 = 18650 battery holder [package=battery-18650-kit]
  BAT2 = 18650 battery holder [package=battery-18650-kit]
  BAT3 = 18650 battery holder [package=battery-18650-kit]
  M1 = Getriebemotor
  M2 = Getriebemotor
  U1 = SWITCH-SPST-2 [package=r_sw_th]
  Componente2 = Bluetooth HC-05 Macho
  JACK1 = 2.1mm Barrel Jack with Terminal Block
  JACK2 = 2.1mm Barrel Jack with Terminal Block

nets:
  N1: Componente1.D2, Componente2.RXD
  N2: Componente1.D3, Componente2.TXD
  N3: Componente1.D6, L298N1.ENB
  N4: Componente1.D7, L298N1.IN4
  N5: Componente1.D8, L298N1.IN3
  N6: Componente1.D9, L298N1.IN2
  N7: Componente1.D10, L298N1.IN1
  N8: Componente1.D11/MOSI, L298N1.ENA
  N9: L298N1.OUT1, M1.pin_2
  N10: L298N1.OUT2, M1.pin_1
  N11: L298N1.OUT3, M2.pin_2
  N12: L298N1.OUT4, M2.pin_1
  N13: L298N1.12V, U1.P
  N14: L298N1.GND, JACK1.NEG
  N15: BAT1.+, JACK2.POS
  N16: BAT1.-, BAT2.+
  N17: BAT3.-, JACK2.NEG
  N18: U1.O, JACK1.POS

custom parts:
  L298N DC motor driver: 2x DC motor driver with 78M05 positive voltage regulator (7..35 V) L298N: max 46 V, 2 A Set 5 V Enable jumper to enable 5 V regultor (needed for the L298N) and +5 V output at screw terminal or supply external +5 V at screw terminal Set ENA and/or ENB to +5 V to enable motor permanently or supply ENA and/or ENB with PWM signal IN1 and IN2 set rotation directory for motor A (OUT1/OUT2) IN2 and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
  18650 battery holder: 18650 Battery Holder
