# Fritzing sketch botsito mixto (saved by Fritzing 0.9.3b)

parts:
  Componente1 = Arduino Nano (Rev3.0)
  L298N1 = L298N DC motor driver
  BAT1 = 18650 battery holder [package=battery-18650-kit]
  BAT2 = 18650 battery holder [package=battery-18650-kit]
  BAT3 = 18650 battery holder [package=battery-18650-kit]
  M1 = Getriebemotor
  M2 = Getriebemotor
  U1 = SWITCH-SPST-2 [package=r_sw_th]
  Componente2 = Bluetooth HC-05 Macho
  JACK1 = 2.1mm Barrel Jack with Terminal Block
  JACK2 = 2.1mm Barrel Jack with Terminal Block
  Componente3 = SRF05 Ultrasonic Rangefinder
  Componente4 = SRF05 Ultrasonic Rangefinder
  S3 = SWITCH-MOMENTARY-2 [package=tactile-pth]
  S4 = SWITCH-MOMENTARY-2 [package=tactile-pth]
  R1 = Resistor [tolerance=±5% resistance=100k package="2512 [SMD]"]
  R2 = Resistor [tolerance=±5% resistance=100k package="2512 [SMD]"]

nets:
  GND: Componente1.GND, Componente2.GND, R1.Pin_1, R2.Pin_1
  N1: Componente1.D5, Componente2.RXD
  N2: Componente1.D6, Componente2.TXD
  N3: Componente1.D7, L298N1.ENB
  N4: Componente1.D8, L298N1.IN4
  N5: Componente1.D9, L298N1.IN3
  N6: Componente1.D10, L298N1.IN2
  N7: Componente1.D11/MOSI, L298N1.IN1
  N8: Componente1.D12/MISO, L298N1.ENA
  5V: Componente1.5V, Componente2.VCC
  N9: Componente1.A5, S4.1
  N10: Componente1.A4, S3.1
  N11: Componente1.A3, Componente4.Trig
  N12: Componente1.A2, Componente4.Echo
  N13: Componente1.A1, Componente3.Trig
  N14: Componente1.A0, Componente3.Echo
  N15: L298N1.OUT1, M1.pin_2
  N16: L298N1.OUT2, M1.pin_1
  N17: L298N1.OUT3, M2.pin_2
  N18: L298N1.OUT4, M2.pin_1
  N19: L298N1.12V, U1.P
  N20: L298N1.GND, JACK1.NEG
  N21: BAT1.+, JACK2.POS
  N22: BAT1.-, BAT2.+
  N23: BAT3.-, JACK2.NEG
  N24: U1.O, JACK1.POS
  VCC: Componente3.VCC, Componente4.VCC
  GND_2: Componente3.GND, Componente4.GND

custom parts:
  L298N DC motor driver: 2x DC motor driver with 78M05 positive voltage regulator (7..35 V) L298N: max 46 V, 2 A Set 5 V Enable jumper to enable 5 V regultor (needed for the L298N) and +5 V output at screw terminal or supply external +5 V at screw terminal Set ENA and/or ENB to +5 V to enable motor permanently or supply ENA and/or ENB with PWM signal IN1 and IN2 set rotation directory for motor A (OUT1/OUT2) IN2 and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
  18650 battery holder: 18650 Battery Holder
