# Fritzing sketch CONTENEDOR (saved by Fritzing 0.9.3b)

parts:
  U3 = Voltage Regulator - 5V [package="TO220 [THT]"]
  U4 = Voltage Regulator -- 3.3 V -- LM1117
  C1 = Ceramic Capacitor [capacitance=330nF package="100 mil [THT, multilayer]"]
  C2 = Ceramic Capacitor [capacitance=100nF package="100 mil [THT, multilayer]"]
  C3 = Tantalum Capacitor [capacitance=10µF package="100 mil [THT, tantalum]"]
  C4 = Tantalum Capacitor [capacitance=10µF package="100 mil [THT, tantalum]"]
  Componente1 = SRF05 Ultrasonic Rangefinder  # not connected
  Componente2 = SRF05 Ultrasonic Rangefinder  # not connected
  M1 = DOIT Esp32 DevKit v1 (30 pins long, 11 pins width) [part_number=ESP32S-PIN30]  # not connected
  J1 = Basic Servo  # not connected
  J2 = Basic Servo  # not connected
  VCC1 = Battery
  A1 = battery capcity indicator module 1s-8s [package=THT]
  J3 = Piezo Speaker
  A2 = TDA2030A module
  WS2812B1 = WS2812B 12V Strip -- White (60/m)  # not connected

nets:
  N1: U3.input_voltage, C1.0
  N2: U3.GND, C1.1, C2.1
  N3: U3.output_voltage, C2.0
  N4: U4.GND, C3.-, C4.-
  N5: U4.OUT, C3.+
  N6: U4.IN, C4.+
  N7: VCC1.-, A1.pin1
  N8: VCC1.+, A1.pin2
  N9: J3.pin1, A2.Pin_6
  N10: J3.pin2, A2.Pin_5

custom parts:
  Voltage Regulator -- 3.3 V -- LM1117: LM1117-3.3 Voltage regulator, 3.3 V output. Note that the pinout order is not the same as LM7805 or LM7833.
  DOIT Esp32 DevKit v1 (30 pins long, 11 pins width): The DOIT Esp32 DevKit v1 is one of the development board created by DOIT to evaluate the ESP-WROOM-32 module. It is based on the ESP32 microcontroller that boasts Wifi, Bluetooth, Ethernet and Low Power support all in a single chip. (vanepp) made breadboard work, adjusted pin numbering and labels and reduced size of schematic and cleaned up pcb. This chip is 30pins long (2 x15) and 11 pins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
  Battery: Your standard 3x 18650 battery pack (11.1 Volts)
  battery capcity indicator module 1s-8s: battery capcity indicator module 1s-8s.
  TDA2030A module: This Module is based on the TDA2030 Audio Amplifier Module which is capable of 18-watt power output with very low harmonic distortion.
  WS2812B 12V Strip -- White (60/m): WS2812B LED Strip, White, 60 pixels per meter, 12V Power
