# Fritzing sketch EsquemaFritzing (saved by Fritzing 0.9.3b)

parts:
  M1 = DOIT Esp32 DevKit v1 (30 pins long, 11 pins width) [part_number=ESP32S-PIN30]
  VCC1 = Battery
  U1 = Voltage Regulator -- 3.3 V -- LM1117
  C1 = Tantalum Capacitor [capacitance=1μF package="100 mil [THT, tantalum]"]
  C2 = Tantalum Capacitor [capacitance=1μF package="100 mil [THT, tantalum]"]
  PART1 = Motor Driver 1A Dual TB6612FNG [part_number=ROB_09457]
  DHT1 = DHT11 Humitidy and Temperature Sensor
  Componente1 = FC-28 Soil Hygrometer Module - Probe
  Componente2 = FC-28 Soil Hygrometer Module
  OLED1 = OLED 128x64 I2C Monochrome Display GND-VDD
  WATER_PUMP1 = water pump/motor
  WATER_PUMP2 = water pump/motor

nets:
  3V3: M1.3V3, OLED1.VDD
  GND: M1.GND, VCC1.-, U1.GND, C1.-, C2.-, PART1.GND, DHT1.GND, Componente2.GND
  N1: M1.D15, DHT1.DATA
  N2: M1.D2, PART1.PWMA
  N3: M1.D4, PART1.PWMB
  N4: M1.D5, PART1.AIN1
  N5: M1.D18, Componente2.AO
  N6: M1.D22, OLED1.SCK
  N7: M1.D26, OLED1.SDA
  N8: M1.D14, PART1.BIN2
  N9: M1.D12, PART1.AIN2
  N10: M1.D13, PART1.BIN1
  N11: VCC1.+, U1.IN, C1.+, PART1.VM
  VCC: U1.OUT, C2.+, PART1.STBY, PART1.VCC, DHT1.VDD, Componente2.VCC
  N12: PART1.A01, WATER_PUMP2.pin_1
  N13: PART1.A02, WATER_PUMP2.pin_2
  N14: PART1.B02, WATER_PUMP1.pin_1
  N15: PART1.B01, WATER_PUMP1.pin_2
  N16: Componente1.POS, Componente2.POS
  N17: Componente1.NEG, Componente2.NEG

custom parts:
  DOIT Esp32 DevKit v1 (30 pins long, 11 pins width): The DOIT Esp32 DevKit v1 is one of the development board created by DOIT to evaluate the ESP-WROOM-32 module. It is based on the ESP32 microcontroller that boasts Wifi, Bluetooth, Ethernet and Low Power support all in a single chip. (vanepp) made breadboard work, adjusted pin numbering and labels and reduced size of schematic and cleaned up pcb. This chip is 30pins long (2 x15) and 11 pins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
  Battery: Your standard 3x 18650 battery pack (11.1 Volts)
  Voltage Regulator -- 3.3 V -- LM1117: LM1117-3.3 Voltage regulator, 3.3 V output. Note that the pinout order is not the same as LM7805 or LM7833.
  Motor Driver 1A Dual TB6612FNG: The TB6612FNG motor driver can control up to two DC motors at a constant current of 1.2A (3.2A peak). Two input signals (IN1 and IN2) can be used to control the motor in one of four function modes - CW, CCW, short-brake, and stop. The two motor outputs (A and B) can be separately controlled, the speed of each motor is controlled via a PWM input signal with a frequency up to 100kHz. The STBY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
  DHT11 Humitidy and Temperature Sensor: DHT11 Humidity and Temperature Sensor
  FC-28 Soil Hygrometer Module - Probe: The FC-28 is a soil hygrometer module that uses the Texas Instruments LM393 comparator chip to provide an analog measurement of soil humidity.
  FC-28 Soil Hygrometer Module: The FC-28 is a soil hygrometer module that uses the Texas Instruments LM393 comparator chip to provide an analog measurement of soil humidity. The digital output is high when soil moisture is over a certain threshold, as determined by adjusting the potentiometer.
  OLED 128x64 I2C Monochrome Display GND-VDD: OLED 128x64 I2C Monochrome Display. Note: there are two variants of this part, this one is the GND VDD SCK SDA variant. The other is VDD GND SCK SDA. Make sure you select the part that matches your module as using the incorrect part will probably destroy your module! In addition the mounting holes are marked on silkscreen but not by default drilled. If you want drilled mounting holes, copy a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
  water pump/motor: WATER PUMP BY ARDUBLOCKTR
